// Logisim project adder4.circ as structural Verilog: 1 circuit, main circuit implementation
module implementation (
  input  [3:0] A_In,
  input  [3:0] B_in,
  input  C_in,
  output [3:0] RESULT_OUT,
  output C_out
);

  wire and_1_out, and_2_out, and_3_out, and_4_out, and_5_out, and_6_out, and_7_out, and_8_out, or_1_out,
       or_2_out, or_3_out, xor_1_out, xor_2_out, xor_3_out, xor_4_out;

  xor xor_1 (xor_1_out, A_In[0], B_in[0]);
  and and_1 (and_1_out, A_In[0], B_in[0]);
  xor xor_2 (xor_2_out, A_In[1], B_in[1]);
  and and_2 (and_2_out, A_In[1], B_in[1]);
  xor xor_3 (xor_3_out, A_In[2], B_in[2]);
  and and_3 (and_3_out, A_In[2], B_in[2]);
  xor xor_4 (xor_4_out, A_In[3], B_in[3]);
  and and_4 (and_4_out, A_In[3], B_in[3]);
  xor xor_5 (RESULT_OUT[0], xor_1_out, C_in);
  and and_5 (and_5_out, xor_1_out, C_in);
  xor xor_6 (RESULT_OUT[1], xor_2_out, or_1_out);
  and and_6 (and_6_out, xor_2_out, or_1_out);
  xor xor_7 (RESULT_OUT[2], xor_3_out, or_2_out);
  and and_7 (and_7_out, xor_3_out, or_2_out);
  xor xor_8 (RESULT_OUT[3], xor_4_out, or_3_out);
  and and_8 (and_8_out, xor_4_out, or_3_out);
  or or_1 (or_1_out, and_5_out, and_1_out);
  or or_2 (or_2_out, and_6_out, and_2_out);
  or or_3 (or_3_out, and_7_out, and_3_out);
  or or_4 (C_out, and_8_out, and_4_out);
endmodule
