// Logisim project dff.circ as structural Verilog: 1 circuit, main circuit implementation
module implementation (
  input  D,
  input  clock,
  output Q,
  output barQ
);

  wire nand_1_out, nand_2_out, not_1_out;

  not not_1 (not_1_out, D);
  nand nand_1 (nand_1_out, D, clock);
  nand nand_2 (nand_2_out, not_1_out, clock);
  nand nand_3 (Q, nand_1_out, barQ);
  nand nand_4 (barQ, Q, nand_2_out);
endmodule
