// Logisim project not.circ as structural Verilog: 1 circuit, main circuit implementation
module implementation (
  input  in_1,
  output out_2
);

  nand nand_1 (out_2, in_1, in_1);
endmodule
