// Logisim project xor.circ as structural Verilog: 1 circuit, main circuit implementation
module implementation (
  input  in_1,
  input  in_2,
  output out_3
);

  wire nand_1_out, nand_2_out, nand_3_out, nand_4_out;

  nand nand_1 (nand_1_out, in_1, in_1);
  nand nand_2 (nand_2_out, in_2, in_2);
  nand nand_3 (nand_3_out, nand_1_out, in_2);
  nand nand_4 (nand_4_out, in_1, nand_2_out);
  nand nand_5 (out_3, nand_3_out, nand_4_out);
endmodule
