// Logisim project alu.circ as structural Verilog: 1 circuit, main circuit implementation
module implementation (
  input  [3:0] ALU_OP_IN,
  input  [3:0] A_In,
  input  [3:0] B_In,
  output [3:0] RESULT_OUT
);

  wire [3:0] adder_1_out, and_1_out, multiplexer_1_out, multiplexer_2_out, multiplexer_3_out,
       multiplexer_4_out, multiplexer_5_out, multiplexer_6_out, multiplexer_7_out, multiplexer_8_out,
       multiplexer_9_out, multiplexer_10_out, multiplexer_11_out, multiplexer_12_out, multiplexer_13_out,
       negator_1_out, not_1_out, or_1_out, subtractor_1_out, xor_1_out;

  assign and_1_out = A_In & B_In;  // AND_Gate and_1, 4 bits wide
  assign or_1_out = A_In | B_In;  // OR_Gate or_1, 4 bits wide
  assign xor_1_out = A_In ^ B_In;  // XOR_Gate xor_1, 4 bits wide
  assign not_1_out = ~A_In;  // NOT_Gate not_1, 4 bits wide
  Negator #(.width(4)) negator_1 (.in(A_In), .out(negator_1_out));
  Adder #(.width(4)) adder_1 (.a(A_In), .b(B_In), .out(adder_1_out));  // open: cin, cout
  Subtractor #(.width(4)) subtractor_1 (.a(A_In), .b(B_In), .out(subtractor_1_out));  // open: bin, bout
  Multiplexer #(.width(4)) multiplexer_1 (.in0(B_In), .in1(A_In), .out(multiplexer_1_out), .sel(ALU_OP_IN[0]));
  Multiplexer #(.width(4)) multiplexer_2 (
    .in0(multiplexer_1_out), .in1(multiplexer_3_out), .out(multiplexer_2_out), .sel(ALU_OP_IN[1]));
  Multiplexer #(.width(4)) multiplexer_3 (.in0(and_1_out), .in1(or_1_out), .out(multiplexer_3_out), .sel(ALU_OP_IN[0]));
  Multiplexer #(.width(4)) multiplexer_4 (
    .in0(xor_1_out), .in1(not_1_out), .out(multiplexer_4_out), .sel(ALU_OP_IN[0]));
  Multiplexer #(.width(4)) multiplexer_5 (
    .in0(multiplexer_4_out), .in1(multiplexer_6_out), .out(multiplexer_5_out), .sel(ALU_OP_IN[1]));
  Multiplexer #(.width(4)) multiplexer_6 (
    .in0(negator_1_out), .out(multiplexer_6_out), .sel(ALU_OP_IN[0]));  // open: in1
  Multiplexer #(.width(4)) multiplexer_7 (
    .in0(multiplexer_11_out), .in1(adder_1_out), .out(multiplexer_7_out), .sel(ALU_OP_IN[0]));
  Multiplexer #(.width(4)) multiplexer_8 (
    .in0(multiplexer_11_out), .in1(multiplexer_7_out), .out(multiplexer_8_out), .sel(ALU_OP_IN[1]));
  Multiplexer #(.width(4)) multiplexer_9 (
    .in0(multiplexer_11_out), .in1(subtractor_1_out), .out(multiplexer_9_out), .sel(ALU_OP_IN[0]));
  Multiplexer #(.width(4)) multiplexer_10 (
    .in0(multiplexer_11_out), .in1(multiplexer_9_out), .out(multiplexer_10_out), .sel(ALU_OP_IN[1]));
  Multiplexer #(.width(4)) multiplexer_11 (
    .in0(multiplexer_2_out), .in1(multiplexer_5_out), .out(multiplexer_11_out), .sel(ALU_OP_IN[2]));
  Multiplexer #(.width(4)) multiplexer_12 (
    .in0(multiplexer_11_out), .in1(multiplexer_8_out), .out(multiplexer_12_out), .sel(ALU_OP_IN[2]));
  Multiplexer #(.width(4)) multiplexer_13 (
    .in0(multiplexer_11_out), .in1(multiplexer_10_out), .out(multiplexer_13_out), .sel(ALU_OP_IN[2]));
  Multiplexer #(.width(4)) multiplexer_14 (
    .in0(multiplexer_12_out), .in1(multiplexer_13_out), .out(RESULT_OUT), .sel(ALU_OP_IN[3]));
endmodule
