// Logisim project UpDownCounter.circ as structural Verilog: 1 circuit, main circuit implementation
module implementation (
  input  Enable,
  input  CountUp,
  input  CountDown,
  output [2:0] Count
);

  wire clock_1_out;
  wire [2:0] adder_1_out, multiplexer_1_out, multiplexer_2_out, multiplexer_3_out, subtractor_1_out;

  Clock clock_1 (.out(clock_1_out));
  Adder #(.width(3)) adder_1 (.a(Count), .b(3'b001), .out(adder_1_out));  // open: cin, cout
  Subtractor #(.width(3)) subtractor_1 (.a(Count), .b(3'b001), .out(subtractor_1_out));  // open: bin, bout
  Multiplexer #(.select(3), .width(3)) multiplexer_1 (
    .in0(adder_1_out), .in1(adder_1_out), .in2(adder_1_out), .in3(adder_1_out), .in4(adder_1_out),
    .in5(adder_1_out), .in6(adder_1_out), .in7(Count), .out(multiplexer_1_out), .sel(Count));
  Multiplexer #(.select(3), .width(3)) multiplexer_2 (
    .in0(Count), .in1(subtractor_1_out), .in2(subtractor_1_out), .in3(subtractor_1_out),
    .in4(subtractor_1_out), .in5(subtractor_1_out), .in6(subtractor_1_out), .in7(subtractor_1_out),
    .out(multiplexer_2_out), .sel(Count));
  Multiplexer #(.select(2), .width(3)) multiplexer_3 (
    .in0(Count), .in1(multiplexer_1_out), .in2(multiplexer_2_out), .in3(Count), .out(multiplexer_3_out),
    .sel({CountDown, CountUp}));
  Register #(.width(3)) register_1 (.D(multiplexer_3_out), .en(Enable), .clk(clock_1_out), .Q(Count));  // open: clr
endmodule
