// Logisim project Vending.circ as structural Verilog: 1 circuit, main circuit implementation
module implementation (
  input  Enable,
  input  Quarter,
  input  Dime,
  input  Nickel,
  output Give_Merchandise,
  output Give_Dime,
  output Give_Nickel
);

  wire clock_1_out, comparator_1_eq, comparator_1_gt, comparator_2_eq, comparator_2_gt, comparator_2_lt,
       comparator_3_eq, comparator_3_gt;
  wire [5:0] adder_1_out, multiplexer_1_out, multiplexer_2_out, multiplexer_3_out, multiplexer_4_out,
       register_1_q, subtractor_1_out, subtractor_2_out;

  Clock clock_1 (.out(clock_1_out));
  Multiplexer #(.select(3), .width(6)) multiplexer_1 (
    .in0({6{1'b0}}), .in1(6'b011001), .in2(6'b001010), .in3({6{1'b0}}), .in4(6'b000101), .in5({6{1'b0}}),
    .in6({6{1'b0}}), .in7({6{1'b0}}), .out(multiplexer_1_out), .sel({Nickel, Dime, Quarter}));
  Adder #(.width(6)) adder_1 (.a(register_1_q), .b(multiplexer_1_out), .out(adder_1_out));  // open: cin, cout
  Comparator #(.mode("unsigned"), .width(6)) comparator_1 (
    .a(adder_1_out), .b(6'b011110), .gt(comparator_1_gt), .eq(comparator_1_eq));  // open: lt
  Subtractor #(.width(6)) subtractor_1 (.a(adder_1_out), .b(6'b011110), .out(subtractor_1_out));  // open: bin, bout
  Register #(.width(6)) register_1 (
    .D(multiplexer_3_out), .en(Enable), .clk(clock_1_out), .Q(register_1_q));  // open: clr
  or or_1 (Give_Merchandise, comparator_1_gt, comparator_1_eq);
  Multiplexer #(.width(6)) multiplexer_2 (
    .in0({6{1'b0}}), .in1(subtractor_1_out), .out(multiplexer_2_out), .sel(Give_Merchandise));
  Multiplexer #(.width(6)) multiplexer_3 (
    .in0(adder_1_out), .in1({6{1'b0}}), .out(multiplexer_3_out), .sel(Give_Merchandise));
  Comparator #(.mode("unsigned"), .width(6)) comparator_2 (
    .a(multiplexer_2_out), .b(6'b001010), .gt(comparator_2_gt), .eq(comparator_2_eq), .lt(comparator_2_lt));
  Subtractor #(.width(6)) subtractor_2 (
    .a(multiplexer_2_out), .b(6'b001010), .out(subtractor_2_out));  // open: bin, bout
  Comparator #(.mode("unsigned"), .width(6)) comparator_3 (
    .a(multiplexer_4_out), .b(6'b000101), .gt(comparator_3_gt), .eq(comparator_3_eq));  // open: lt
  or or_2 (Give_Dime, comparator_2_gt, comparator_2_eq);
  Multiplexer #(.width(6)) multiplexer_4 (
    .in0(subtractor_2_out), .in1(multiplexer_2_out), .out(multiplexer_4_out), .sel(comparator_2_lt));
  or or_3 (Give_Nickel, comparator_3_gt, comparator_3_eq);
endmodule
