// Logisim project CPU.circ as structural Verilog: 1 circuit, main circuit main
module main (
  output [7:0] print_R0,
  output [7:0] print_R1,
  output halt
);

  wire ALU0, ALU1, and_1_out, and_2_out, and_3_out, and_4_out, and_5_out, and_7_out, and_8_out, and_9_out,
       and_10_out, Buss, clock_1_out, comparator_1_eq, comparator_2_eq, IRin, IRout, MARin, MDRout, MemRead,
       not_1_out, not_2_out, Offset, ONEout, or_1_out, PCin, PCout, R0in, R0out, R1in, R1out, Rdsin, Rdsout,
       Rsout, State0, State2, State4, State5, State6, State7, State8, State9, State10, State12, State13,
       State14, State15, State16, State17, State18, State19, State20, State21, State22, Xin, Zin, Zout;
  wire [2:0] controlled_buffer_4_out;
  wire [4:0] bit_extender_1_out, multiplexer_1_out, multiplexer_2_out, register_1_q;
  wire [7:0] adder_1_out, controlled_buffer_1_out, controlled_buffer_2_out, controlled_buffer_3_out,
       controlled_buffer_6_out, controlled_buffer_7_out, controlled_buffer_9_out, controlled_buffer_11_out,
       controlled_buffer_13_out, controlled_buffer_16_out, IR, MAR_q, MDR_q, multiplexer_3_out,
       multiplexer_4_out, multiplier_1_out, nand_1_out, PC, ram_1_dout, subtractor_1_out, X_q, Z_q;
  wire [7:3] controlled_buffer_4_out_2;

  Clock clock_1 (.out(clock_1_out));
  assign controlled_buffer_1_out = PCin ? {controlled_buffer_4_out_2, controlled_buffer_4_out} : 8'bz;  // Controlled_Buffer controlled_buffer_1
  assign controlled_buffer_2_out = 1'b0 ? {controlled_buffer_4_out_2, controlled_buffer_4_out} : 8'bz;  // Controlled_Buffer controlled_buffer_2
  or or_1 (or_1_out, 1'b0, MemRead);
  assign controlled_buffer_3_out = 1'b0 ? MDR_q : 8'bz;  // Controlled_Buffer controlled_buffer_3
  Register u_PC (.D(controlled_buffer_1_out), .en(PCin), .clk(clock_1_out), .Q(PC));  // open: clr
  Register #(.trigger("high")) MDR (
    .D(controlled_buffer_2_out), .en(or_1_out), .clk(clock_1_out), .Q(MDR_q));  // open: clr
  RAM ram_1 (
    .addr(MAR_q), .we(1'b0), .oe(MemRead), .clk(clock_1_out), .din(controlled_buffer_3_out), .dout(ram_1_dout));
  assign {controlled_buffer_4_out_2, controlled_buffer_4_out} = PCout ? PC : 8'bz;  // Controlled_Buffer controlled_buffer_4
  assign {controlled_buffer_4_out_2, controlled_buffer_4_out} = MDRout ? MDR_q : 8'bz;  // Controlled_Buffer controlled_buffer_5
  Register #(.width(5)) register_1 (
    .D(multiplexer_1_out), .en(1'b1), .clk(clock_1_out), .Q(register_1_q));  // open: clr
  Multiplexer #(.select(5), .width(5)) multiplexer_1 (
    .in0(5'b00001), .in1(5'b00010), .in2(5'b00011), .in3(multiplexer_2_out), .in4(5'b00101), .in5(5'b00110),
    .in6({5{1'b0}}), .in7(5'b01000), .in8(5'b01001), .in9({5{1'b0}}), .in10(5'b01011), .in11(5'b01100),
    .in12({5{1'b0}}), .in13(5'b01110), .in14(5'b01111), .in15(5'b10000), .in16({5{1'b0}}), .in17(5'b10010),
    .in18(5'b10011), .in19({5{1'b0}}), .in20(5'b10101), .in21(5'b10110), .in22({5{1'b0}}),
    .out(multiplexer_1_out), .sel(register_1_q));  // open: in23, in24, in25, in26, in27, in28, in29, in30, in31
  Register #(.trigger("high")) u_IR (.D(controlled_buffer_6_out), .en(IRin), .clk(clock_1_out), .Q(IR));  // open: clr
  assign controlled_buffer_6_out = IRin ? {controlled_buffer_4_out_2, controlled_buffer_4_out} : 8'bz;  // Controlled_Buffer controlled_buffer_6
  assign controlled_buffer_7_out = MARin ? {controlled_buffer_4_out_2, controlled_buffer_4_out} : 8'bz;  // Controlled_Buffer controlled_buffer_7
  Register MAR (.D(controlled_buffer_7_out), .en(MARin), .clk(clock_1_out), .Q(MAR_q));  // open: clr
  assign controlled_buffer_2_out = MemRead ? ram_1_dout : 8'bz;  // Controlled_Buffer controlled_buffer_8
  Multiplexer #(.select(4), .width(5)) multiplexer_2 (
    .in0(5'b10001), .in1(5'b00100), .in2(5'b01101), .in3(5'b00111), .in4(5'b10100), .in15(5'b01010),
    .out(multiplexer_2_out), .sel(IR[7:4]));  // open: in5, in6, in7, in8, in9, in10, in11, in12, in13, in14
  assign controlled_buffer_9_out = R0in ? {controlled_buffer_4_out_2, controlled_buffer_4_out} : 8'bz;  // Controlled_Buffer controlled_buffer_9
  assign {controlled_buffer_4_out_2, controlled_buffer_4_out} = IRout ? IR : 8'bz;  // Controlled_Buffer controlled_buffer_10
  Register R0 (.D(controlled_buffer_9_out), .en(R0in), .clk(clock_1_out), .Q(print_R0));  // open: clr
  and and_1 (and_1_out, controlled_buffer_4_out_2[3], Offset);
  Demultiplexer #(.select(5)) demultiplexer_1 (
    .out0(State0), .out1(ONEout), .out2(State2), .out3(IRin), .out4(State4), .out5(State5), .out6(State6),
    .out7(State7), .out8(State8), .out9(State9), .out10(State10), .out11(Offset), .out12(State12),
    .out13(State13), .out14(State14), .out15(State15), .out16(State16), .out17(State17), .out18(State18),
    .out19(State19), .out20(State20), .out21(State21), .out22(State22), .in(1'b1), .sel(register_1_q));  // open: out23, out24, out25, out26, out27, out28, out29, out30, out31
  assign bit_extender_1_out = {{4{and_1_out}}, and_1_out};  // Bit_Extender bit_extender_1
  Multiplexer #(.width(8)) multiplexer_3 (
    .in0({bit_extender_1_out, controlled_buffer_4_out}),
    .in1({controlled_buffer_4_out_2, controlled_buffer_4_out}), .out(multiplexer_3_out), .sel(Buss));
  // Probe on X_q
  // Probe on multiplexer_3_out
  assign controlled_buffer_11_out = R1in ? {controlled_buffer_4_out_2, controlled_buffer_4_out} : 8'bz;  // Controlled_Buffer controlled_buffer_11
  assign {controlled_buffer_4_out_2, controlled_buffer_4_out} = R0out ? print_R0 : 8'bz;  // Controlled_Buffer controlled_buffer_12
  assign controlled_buffer_13_out = Xin ? {controlled_buffer_4_out_2, controlled_buffer_4_out} : 8'bz;  // Controlled_Buffer controlled_buffer_13
  assign nand_1_out = ~(X_q & multiplexer_3_out);  // NAND_Gate nand_1, 8 bits wide
  Subtractor subtractor_1 (.a(X_q), .b(multiplexer_3_out), .out(subtractor_1_out));  // open: bin, bout
  Multiplier multiplier_1 (.a(X_q), .b(multiplexer_3_out), .out(multiplier_1_out));  // open: cin, cout
  Adder adder_1 (.a(X_q), .b(multiplexer_3_out), .out(adder_1_out));  // open: cin, cout
  Register R1 (.D(controlled_buffer_11_out), .en(R1in), .clk(clock_1_out), .Q(print_R1));  // open: clr
  Register X (.D(controlled_buffer_13_out), .en(Xin), .clk(clock_1_out), .Q(X_q));  // open: clr
  assign {controlled_buffer_4_out_2, controlled_buffer_4_out} = R1out ? print_R1 : 8'bz;  // Controlled_Buffer controlled_buffer_14
  Multiplexer #(.select(2), .width(8)) multiplexer_4 (
    .in0(nand_1_out), .in1(subtractor_1_out), .in2(multiplier_1_out), .in3(adder_1_out),
    .out(multiplexer_4_out), .sel({ALU1, ALU0}));
  not not_1 (not_1_out, IR[2]);
  not not_2 (not_2_out, IR[3]);
  assign {controlled_buffer_4_out_2, controlled_buffer_4_out} = ONEout ? 8'h1 : 8'bz;  // Controlled_Buffer controlled_buffer_15
  assign controlled_buffer_16_out = Zin ? multiplexer_4_out : 8'bz;  // Controlled_Buffer controlled_buffer_16
  or or_2 (PCin, State2, State12);
  or or_3 (Rdsin, State6, State9, State16, State19, State22);
  or or_4 (Zin, ONEout, State5, State8, Offset, State15, State18, State21);
  or or_5 (Zout, State2, State6, State9, State12, State16, State19, State22);
  and and_2 (and_2_out, Rdsin, not_2_out);
  or or_6 (R0in, and_2_out, and_3_out);
  and and_3 (and_3_out, 1'b0, not_1_out);
  and and_4 (and_4_out, Rdsout, not_2_out);
  or or_7 (R0out, and_4_out, and_5_out);
  and and_5 (and_5_out, Rsout, not_1_out);
  Register #(.trigger("high")) Z (.D(controlled_buffer_16_out), .en(Zin), .clk(clock_1_out), .Q(Z_q));  // open: clr
  Comparator comparator_1 (.a(PC), .b(8'hf), .eq(comparator_1_eq));  // open: gt, lt
  Comparator comparator_2 (.a(IR), .b({8{1'b0}}), .eq(comparator_2_eq));  // open: gt, lt
  and and_6 (halt, comparator_1_eq, comparator_2_eq);
  or or_8 (MARin, State0, State13);
  or or_9 (Xin, State0, State4, State7, State10, State14, State17, State20);
  or or_10 (ALU0, ONEout, State5, State8, Offset, State15, State21);
  or or_11 (ALU1, ONEout, State5, State8, Offset, State15);
  or or_12 (MemRead, State0, ONEout, State2, State13, State14);
  and and_7 (and_7_out, Rdsin, IR[3]);
  and and_8 (and_8_out, 1'b0, IR[2]);
  and and_9 (and_9_out, Rdsout, IR[3]);
  and and_10 (and_10_out, Rsout, IR[2]);
  // Probe on {controlled_buffer_4_out_2, controlled_buffer_4_out}
  assign {controlled_buffer_4_out_2, controlled_buffer_4_out} = Zout ? Z_q : 8'bz;  // Controlled_Buffer controlled_buffer_17
  or or_13 (R1in, and_7_out, and_8_out);
  or or_14 (R1out, and_9_out, and_10_out);
  or or_15 (Buss, ONEout, State5, State15, State18, State21);
  or or_16 (PCout, State0, State10);
  or or_17 (IRout, State8, Offset);
  or or_18 (Rdsout, State4, State7, State14, State17, State20);
  or or_19 (Rsout, State5, State13, State18, State21);
  or or_20 (MDRout, IRin, State15);

  // Other names for the same wires on the sheet: R0[7:0] = print_R0; R1[7:0] = print_R1; State1 = ONEout;
  //   State3 = IRin; State11 = Offset
endmodule
